# Fritzing sketch Arduino_ESP8266_DHT22 (saved by Fritzing 0.9.3b)
breadboards: 1

parts:
  U1 = ESP8266 ESP-01 Upgraded WiFi Module [part_number=ESP8266]  # not connected
  Part1 = Arduino Nano (Rev3.0)
  DHT1 = DHT22 Humidity and Temperature Sensor
  R1 = Resistor [tolerance=±5% resistance=10k package=THT]

nets:
  GND: Part1.GND, DHT1.GND
  N1: Part1.D5, DHT1.DATA, R1.Pin_0
  3V3: Part1.3V3, DHT1.VDD, R1.Pin_1

custom parts:
  ESP8266 ESP-01 Upgraded WiFi Module: Upgraded Version ESP-01,all Flash are upgraded to 1M byte.Also support Cloud service remote transmission.
